# Fritzing sketch talking-treasure-chest-electronics (saved by Fritzing 0.9.3b)

parts:
  Part1 = Arduino Uno (Rev3)
  Part2 = Real Time Clock Module - DS1307 RTC Breakout Board
  BATT1 = 4xAA Switchable Battery Pack w/Bare Wire
  Part3 = Mono 2.5W Class D Audio Amplifier - PAM8302
  Part5 = Adafruit Audio FX Mini Sound Board [part_number="Adafruit #2342 and #2220"]
  R1 = Resistor [tolerance=±5% resistance=220 package=THT]
  LED1 = LED - 5mm [color="Green (555nm)" package="5 mm [THT]"]
  SPKR1 = Loudspeaker
  J1 = Basic Servo
  Componente2 = RFID-RC522-v2
  S2 = Toggle Switch [package=THT]

nets:
  N1: Part1.A4/SDA, Part2.SDA
  N2: Part1.A5/SCL, Part2.SCL
  N3: Part1.D8, Componente2.RST
  N4: Part1.D9_PWM, J1.pulse
  N5: Part1.D10_PWM/SS, Componente2.SDA
  N6: Part1.D11_PWM/MOSI, Componente2.MOSI
  N7: Part1.D12/MISO, Componente2.MISO
  N8: Part1.D13/SCK, Componente2.SCK
  N9: Part1.D2, S2.L1
  N10: Part1.D3_PWM, Part2.SQW
  N11: Part1.D4, Part5.RST
  N12: Part1.D5_PWM, Part5.TX
  N13: Part1.D6_PWM, Part5.RX_5V
  N14: Part1.D7, LED1.anode
  3V3: Part1.3V3, Componente2.3.3V
  5V: Part1.5V, Part2.5V, Part3.VCC, Part5.VIN
  GND: Part1.GND, Part2.GND, Part5.UG
  N15: BATT1.POS, J1.vcc
  GND_2: BATT1.NEG, Part3.GND, J1.gnd
  GND_3: Part3.AIN-, Part5.GND, Componente2.GND
  N16: Part3.AIN+, Part5.R_AC
  N17: Part3.VO+, SPKR1.pin2
  N18: Part3.VO-, SPKR1.pin1
  N19: R1.Pin_1, S2.COM

custom parts:
  4xAA Switchable Battery Pack w/Bare Wire: 4xAA Switchable Battery Pack with Bare Wire connection
  Mono 2.5W Class D Audio Amplifier - PAM8302: A super small but powerful mono amplifier able to deliver up to 2.5 Watts into 4-8 ohm impedance speakers. Inside the miniature chip is a class D controller, able to run from 2.0V-5.5VDC. Since the amp is a class D, its very efficient (over 90% efficient when driving an 8Ω speaker at over half a Watt) - making it perfect for portable and battery-powered projects.
  Adafruit Audio FX Mini Sound Board: Would you like to add audio/sound effects to your next project, without an Arduino+Shield? Or maybe you don't even know how to use microcontrollers, you just want to make a sound play whenever you press a button. What about something that has to be very small and portable? You are probably feeling a little frustrated: it's been very hard to find a simple, low cost audio effects trigger that is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
  RFID-RC522-v2: A simple China made RFID-RC522 Reader; do check the pin labels, as this is a MFRC522 based clone.
